// Digital circuit Adder.dig as structural Verilog
module Adder (
  input  A0,
  input  B0,
  input  A1,
  input  B1,
  input  A2,
  input  B2,
  input  A3,
  input  B3,
  input  A4,
  input  B4,
  input  A5,
  input  B5,
  input  A6,
  input  B6,
  input  A7,
  input  B7,
  output S0,
  output S1,
  output S2,
  output S3,
  output S4,
  output S5,
  output S6,
  output S7,
  output Ov
);

  wire full_adder_1_p3, full_adder_2_p3, full_adder_3_p3, full_adder_4_p3, full_adder_5_p3, full_adder_6_p3,
       full_adder_7_p3;

  // Full_Adder full_adder_1: pin names not known; wires that end beside it: A7, B7, full_adder_1_p3, S7, Ov
  // Full_Adder full_adder_2: pin names not known; wires that end beside it: A6, B6, full_adder_2_p3, S6, full_adder_1_p3
  // Full_Adder full_adder_3: pin names not known; wires that end beside it: A5, B5, full_adder_3_p3, S5, full_adder_2_p3
  // Full_Adder full_adder_4: pin names not known; wires that end beside it: A4, B4, full_adder_4_p3, S4, full_adder_3_p3
  // Full_Adder full_adder_5: pin names not known; wires that end beside it: A3, B3, full_adder_5_p3, S3, full_adder_4_p3
  // Full_Adder full_adder_6: pin names not known; wires that end beside it: A2, B2, full_adder_6_p3, S2, full_adder_5_p3
  // Full_Adder full_adder_7: pin names not known; wires that end beside it: A1, B1, full_adder_7_p3, S1, full_adder_6_p3
  // Half_Adder half_adder_1: pin names not known; wires that end beside it: A0, B0, S0, full_adder_7_p3
endmodule
