// Digital circuit CPU.dig as structural Verilog
module CPU (
  input  I0,
  input  I1,
  input  I2,
  input  I3,
  input  I4,
  input  I5,
  input  I6,
  input  I7,
  input  A,
  input  B,
  input  C,
  input  D,
  input  WRAM,
  input  RRAM
);

  wire acumulator_1_s0, acumulator_1_s1, acumulator_1_s2, acumulator_1_s3, acumulator_1_s4, acumulator_1_s5,
       acumulator_1_s6, acumulator_1_s7, Clk, Clr, controller_1_hlt, controller_1_l1, controller_1_l2,
       controller_1_l3, controller_1_l4, controller_1_l5, controller_1_l6, Cp, diodeforward_1_out,
       diodeforward_2_out, diodeforward_3_out, Ea, Ep, Eu, instruction_register_1_c0,
       instruction_register_1_c1, instruction_register_1_c2, instruction_register_1_c3,
       instruction_register_1_op0, instruction_register_1_op1, instruction_register_1_op2,
       instruction_register_1_op3, memory_address_register_1_p1, memory_address_register_1_p2,
       memory_address_register_1_p3, memory_address_register_1_p4, NEi, NLa, NLb, NLi, NLm, NLo, Op, Op0,
       Op1, Op2, Ori, pulldown_4_out, pulldown_5_out, ram_1_s0, ram_1_s1, ram_1_s2, ram_1_s3, ram_1_s4,
       ram_1_s5, ram_1_s6, ram_1_s7, READ, register_b_1_s0, register_b_1_s1, register_b_1_s2,
       register_b_1_s3, register_b_1_s4, register_b_1_s5, register_b_1_s6, register_b_1_s7, ula_1_eq,
       ula_1_out_20, ula_1_plus, WRITE, WRITE_out;
  wire [3:0] register_out_1_s0, register_out_1_s4;

  DiodeForward diodeforward_1 (.in(memory_address_register_1_p3), .out(diodeforward_1_out));
  DiodeForward diodeforward_2 (.in(memory_address_register_1_p2), .out(diodeforward_2_out));
  DiodeForward diodeforward_3 (.in(memory_address_register_1_p1), .out(diodeforward_3_out));
  PullDown pulldown_1 (.out(diodeforward_3_out));
  PullDown pulldown_2 (.out(diodeforward_2_out));
  PullDown pulldown_3 (.out(diodeforward_1_out));
  PullDown pulldown_4 (.out(pulldown_4_out));
  PullDown pulldown_5 (.out(pulldown_5_out));
  DiodeForward diodeforward_4 (.in(memory_address_register_1_p4), .out(pulldown_4_out));
  DiodeForward diodeforward_5 (.in(WRITE_out), .out(pulldown_5_out));
  Button u_WRITE (.out(WRITE_out));
  DiodeForward diodeforward_6 (.in(C), .out(diodeforward_2_out));
  DiodeForward diodeforward_7 (.in(D), .out(diodeforward_3_out));
  DiodeForward diodeforward_8 (.in(Clk), .out(pulldown_5_out));
  DiodeForward diodeforward_9 (.in(A), .out(pulldown_4_out));
  DiodeForward diodeforward_10 (.in(B), .out(diodeforward_1_out));
  PullDown pulldown_6 (.out(pulldown_5_out));
  RAM ram_1 (
    .I0(I0), .I1(I1), .I2(I2), .I3(I3), .I4(I4), .I5(I5), .I6(I6), .I7(I7), .READ(READ),
    .Clk(pulldown_5_out), .A(pulldown_4_out), .B(diodeforward_1_out), .C(diodeforward_2_out),
    .D(diodeforward_3_out), .WRITE(WRITE), .Clr(Clr), .S0(ram_1_s0), .S1(ram_1_s1), .S2(ram_1_s2),
    .S3(ram_1_s3), .S4(ram_1_s4), .S5(ram_1_s5), .S6(ram_1_s6), .S7(ram_1_s7));
  Button u_Clk (.out(Clk));
  Button u_Ori (.out(Ori));
  Button u_Clr (.out(Clr));
  DiodeForward diodeforward_11 (.in(instruction_register_1_op0), .out(ram_1_s0));
  DiodeForward diodeforward_12 (.in(instruction_register_1_op1), .out(ram_1_s1));
  DiodeForward diodeforward_13 (.in(instruction_register_1_op2), .out(ram_1_s2));
  DiodeForward diodeforward_14 (.in(instruction_register_1_op3), .out(ram_1_s3));
  Instruction_Register instruction_register_1 (
    .NEi(NEi), .Clr(Clr), .Clk(Clk), .NLi(NLi), .I0(ram_1_s0), .I1(ram_1_s1), .I2(ram_1_s2), .I3(ram_1_s3),
    .I4(ram_1_s4), .I5(ram_1_s5), .I6(ram_1_s6), .I7(ram_1_s7), .Op(Op), .C0(instruction_register_1_c0),
    .C1(instruction_register_1_c1), .C2(instruction_register_1_c2), .C3(instruction_register_1_c3),
    .Op0(instruction_register_1_op0), .Op1(instruction_register_1_op1), .Op2(instruction_register_1_op2),
    .Op3(instruction_register_1_op3));
  Program_Counter program_counter_1 (
    .Cp(Cp), .Ep(Ep), .Clr(Clr), .NClk(Clk), .S0(ram_1_s0), .S1(ram_1_s1), .S2(ram_1_s2), .S3(ram_1_s3));
  Controller controller_1 (
    .Clk(Clk), .Ori(Ori), .I0(instruction_register_1_c0), .I1(instruction_register_1_c1),
    .I2(instruction_register_1_c2), .I3(instruction_register_1_c3), .WRITE(WRAM), .READ(RRAM), .Ep(Ep),
    .Cp(Cp), .NLm(NLm), .NEi(NEi), .WRAM(WRITE), .NLi(NLi), .Ea(Ea), .NLa(NLa), .Op0(Op0), .Op1(Op1),
    .Op2(Op2), .Eu(Eu), .NLb(NLb), .NLo(NLo), .HLT(controller_1_hlt), .RRAM(READ), .L1(controller_1_l1),
    .L2(controller_1_l2), .L3(controller_1_l3), .L4(controller_1_l4), .L5(controller_1_l5),
    .L6(controller_1_l6), .Op(Op));
  // Memory_Address_Register memory_address_register_1: pin names not known; wires that end beside it: memory_address_register_1_p1, memory_address_register_1_p2, memory_address_register_1_p3, memory_address_register_1_p4, Clr, ram_1_s3, ram_1_s2, ram_1_s1, ram_1_s0, Clk, NLm
  PullDown pulldown_7 (.out(ram_1_s7));
  PullDown pulldown_8 (.out(ram_1_s5));
  PullDown pulldown_9 (.out(ram_1_s6));
  LED led_1 (.in(controller_1_l1));
  LED led_2 (.in(controller_1_l2));
  PullDown pulldown_10 (.out(ram_1_s3));
  PullDown pulldown_11 (.out(ram_1_s4));
  LED led_3 (.in(controller_1_l3));
  LED led_4 (.in(controller_1_l4));
  PullDown pulldown_12 (.out(ram_1_s1));
  PullDown pulldown_13 (.out(ram_1_s2));
  LED led_5 (.in(controller_1_l5));
  LED led_6 (.in(controller_1_l6));
  PullDown pulldown_14 (.out(ram_1_s0));
  LED HLT (.in(controller_1_hlt));
  Register_B register_b_1 (
    .NLb(NLb), .Clk(Clk), .I0(ram_1_s0), .I1(ram_1_s1), .I2(ram_1_s2), .I3(ram_1_s3), .I4(ram_1_s4),
    .I5(ram_1_s5), .I6(ram_1_s6), .I7(ram_1_s7), .Clr(Clr), .S0(register_b_1_s0), .S1(register_b_1_s1),
    .S2(register_b_1_s2), .S3(register_b_1_s3), .S4(register_b_1_s4), .S5(register_b_1_s5),
    .S6(register_b_1_s6), .S7(register_b_1_s7));
  Register_OUT register_out_1 (
    .NLo(NLo), .Clk(Clk), .I0(ram_1_s0), .I1(ram_1_s1), .I2(ram_1_s2), .I3(ram_1_s3), .I4(ram_1_s4),
    .I5(ram_1_s5), .I6(ram_1_s6), .I7(ram_1_s7), .Clr(Clr), .S0(register_out_1_s0[0]),
    .S1(register_out_1_s0[1]), .S2(register_out_1_s0[2]), .S3(register_out_1_s0[3]),
    .S4(register_out_1_s4[0]), .S5(register_out_1_s4[1]), .S6(register_out_1_s4[2]), .S7(register_out_1_s4[3]));
  Acumulator acumulator_1 (
    .NLa(NLa), .Ea(Ea), .Clk(Clk), .I0(ram_1_s0), .I1(ram_1_s1), .I2(ram_1_s2), .I3(ram_1_s3), .I4(ram_1_s4),
    .I5(ram_1_s5), .I6(ram_1_s6), .I7(ram_1_s7), .Clr(Clr), .S0(acumulator_1_s0), .S1(acumulator_1_s1),
    .S2(acumulator_1_s2), .S3(acumulator_1_s3), .S4(acumulator_1_s4), .S5(acumulator_1_s5),
    .S6(acumulator_1_s6), .S7(acumulator_1_s7));
  PullDown pulldown_15 (.out(acumulator_1_s0));
  PullDown pulldown_16 (.out(acumulator_1_s1));
  PullDown pulldown_17 (.out(acumulator_1_s2));
  PullDown pulldown_18 (.out(acumulator_1_s3));
  PullDown pulldown_19 (.out(acumulator_1_s4));
  PullDown pulldown_20 (.out(acumulator_1_s5));
  PullDown pulldown_21 (.out(acumulator_1_s6));
  PullDown pulldown_22 (.out(acumulator_1_s7));
  ULA ula_1 (
    .A0(acumulator_1_s0), .B0(register_b_1_s0), .A1(acumulator_1_s1), .B1(register_b_1_s1),
    .A2(acumulator_1_s2), .B2(register_b_1_s2), .A3(acumulator_1_s3), .B3(register_b_1_s3),
    .A4(acumulator_1_s4), .B4(register_b_1_s4), .A5(acumulator_1_s5), .B5(register_b_1_s5),
    .A6(acumulator_1_s6), .B6(register_b_1_s6), .A7(acumulator_1_s7), .B7(register_b_1_s7), .C0(Op0),
    .C1(Op1), .C2(Op2), .Eu(Eu), .out_20(ula_1_out_20), .eq(ula_1_eq), .plus(ula_1_plus), .S0(ram_1_s0),
    .S1(ram_1_s1), .S2(ram_1_s2), .S3(ram_1_s3), .S4(ram_1_s4), .S5(ram_1_s5), .S6(ram_1_s6), .S7(ram_1_s7));
  Seven_Seg_Hex seven_seg_hex_1 (.d(register_out_1_s4), .dp(1'b0));
  Seven_Seg_Hex seven_seg_hex_2 (.d(register_out_1_s0), .dp(1'b0));
  LED plus (.in(ula_1_plus));
  LED led_7 (.in(ula_1_out_20));
  LED eq (.in(ula_1_eq));

  // Notes on the sheet:
  //   0000 - Load
  //   0001 - Sum
  //   0010 - Sub
  //   0011 - Comp
  //   0100 - Multi
  //   0101 - ShiftR
  //   0110 - ShiftL
  //   0111 - OUT
  //   1000 - HLT
endmodule
