// Digital circuit Comparator.dig as structural Verilog
module Comparator (
  input  A0,
  input  B0,
  input  A1,
  input  A2,
  input  A3,
  input  A4,
  input  A5,
  input  A6,
  input  A7,
  input  B1,
  input  B2,
  input  B3,
  input  B4,
  input  B5,
  input  B6,
  input  B7,
  output A_lt_B,
  output A_eq_B,
  output A_gt_B
);

  wire full_comparator_1_p3, full_comparator_1_p4, full_comparator_1_p5, full_comparator_2_p3,
       full_comparator_2_p4, full_comparator_2_p5, full_comparator_3_p3, full_comparator_3_p4,
       full_comparator_3_p5, full_comparator_4_p3, full_comparator_4_p4, full_comparator_4_p5,
       full_comparator_5_p3, full_comparator_5_p4, full_comparator_5_p5, full_comparator_6_p3,
       full_comparator_6_p4, full_comparator_6_p5, full_comparator_7_p3, full_comparator_7_p4,
       full_comparator_7_p5;

  // Full_Comparator full_comparator_1: pin names not known; wires that end beside it: A7, B7, full_comparator_1_p3, full_comparator_1_p4, full_comparator_1_p5, A_lt_B, A_eq_B, A_gt_B
  // Full_Comparator full_comparator_2: pin names not known; wires that end beside it: A6, B6, full_comparator_2_p3, full_comparator_2_p4, full_comparator_2_p5, full_comparator_1_p3, full_comparator_1_p4, full_comparator_1_p5
  // Full_Comparator full_comparator_3: pin names not known; wires that end beside it: A5, B5, full_comparator_3_p3, full_comparator_3_p4, full_comparator_3_p5, full_comparator_2_p3, full_comparator_2_p4, full_comparator_2_p5
  // Full_Comparator full_comparator_4: pin names not known; wires that end beside it: A4, B4, full_comparator_4_p3, full_comparator_4_p4, full_comparator_4_p5, full_comparator_3_p3, full_comparator_3_p4, full_comparator_3_p5
  // Full_Comparator full_comparator_5: pin names not known; wires that end beside it: A3, B3, full_comparator_5_p3, full_comparator_5_p4, full_comparator_5_p5, full_comparator_4_p3, full_comparator_4_p4, full_comparator_4_p5
  // Full_Comparator full_comparator_6: pin names not known; wires that end beside it: A2, B2, full_comparator_6_p3, full_comparator_6_p4, full_comparator_6_p5, full_comparator_5_p3, full_comparator_5_p4, full_comparator_5_p5
  // Full_Comparator full_comparator_7: pin names not known; wires that end beside it: A1, B1, full_comparator_7_p3, full_comparator_7_p4, full_comparator_7_p5, full_comparator_6_p3, full_comparator_6_p4, full_comparator_6_p5
  // Half_Comparator half_comparator_1: pin names not known; wires that end beside it: A0, B0, full_comparator_7_p3, full_comparator_7_p4, full_comparator_7_p5
endmodule
