// Digital circuit Controller.dig as structural Verilog
module Controller (
  input  Clk,
  input  Ori,
  input  I0,
  input  I1,
  input  I2,
  input  I3,
  input  WRITE,
  input  READ,
  output Ep,
  output Cp,
  output NLm,
  output NEi,
  output WRAM,
  output NLi,
  output Ea,
  output NLa,
  output Op0,
  output Op1,
  output Op2,
  output Eu,
  output NLb,
  output NLo,
  output HLT,
  output RRAM,
  output L1,
  output L2,
  output L3,
  output L4,
  output L5,
  output L6,
  output Op
);

  wire and_1_out, and_2_out, and_3_out, and_4_out, and_5_out, and_6_out, and_7_out, and_8_out, and_9_out,
       and_10_out, and_11_out, and_12_out, and_13_out, and_14_out, and_15_out, and_17_out, and_20_out,
       and_21_out, and_22_out, and_23_out, and_24_out, and_25_out, and_26_out, and_27_out, and_28_out,
       and_29_out, and_30_out, and_31_out, and_32_out, and_33_out, and_34_out, and_35_out, and_36_out,
       and_37_out, and_38_out, not_1_out, or_3_out, or_4_out, ring_counter_1_t7, selector_1_s0,
       selector_1_s1, selector_1_s2, selector_1_s3, selector_1_s4, selector_1_s5, selector_1_s6,
       selector_1_s7, selector_1_s8;

  not not_1 (not_1_out, Clk);
  Ring_Counter ring_counter_1 (
    .Clk(not_1_out), .Ori(Ori), .T1(Ep), .T2(Cp), .T3(L3), .T4(L4), .T5(L5), .T6(L6), .T7(ring_counter_1_t7));
  Selector selector_1 (
    .A(I0), .B(I1), .C(I2), .D(I3), .S0(selector_1_s0), .S1(selector_1_s1), .S2(selector_1_s2),
    .S3(selector_1_s3), .S4(selector_1_s4), .S5(selector_1_s5), .S6(selector_1_s6), .S7(selector_1_s7),
    .S8(selector_1_s8));
  nor nor_1 (NLm, L4, Ep);
  or or_1 (WRAM, Cp, WRITE);
  and and_1 (and_1_out, ~selector_1_s7, L5);  // And
  or or_2 (RRAM, and_1_out, READ, L3);
  not not_2 (NLi, L3);
  nor nor_2 (NEi, ring_counter_1_t7, L6, L5, L4);
  and and_2 (and_2_out, selector_1_s0, L5);
  and and_3 (and_3_out, selector_1_s5, L5);
  or or_3 (or_3_out, and_4_out, and_3_out, and_2_out);
  nor nor_3 (NLa, or_4_out, or_3_out);
  and and_4 (and_4_out, selector_1_s6, L5);
  and and_5 (and_5_out, selector_1_s1, L6);
  and and_6 (and_6_out, selector_1_s2, L6);
  and and_7 (and_7_out, selector_1_s3, L6);
  or or_4 (or_4_out, and_10_out, and_9_out, and_8_out, and_7_out, and_6_out, and_5_out);
  or or_5 (Ea, and_14_out, and_13_out, and_12_out, and_11_out);
  and and_8 (and_8_out, selector_1_s4, L6);
  and and_9 (and_9_out, selector_1_s5, L6);
  and and_10 (and_10_out, selector_1_s6, L6);
  and and_11 (and_11_out, selector_1_s0, L6);
  and and_12 (and_12_out, selector_1_s5, L6);
  and and_13 (and_13_out, selector_1_s6, L6);
  and and_14 (and_14_out, selector_1_s7, L6);
  and and_15 (and_15_out, selector_1_s6, selector_1_s2);
  DiodeForward diodeforward_1 (.in(and_15_out), .out(Op2));
  DiodeForward diodeforward_2 (.in(and_15_out), .out(Op0));
  and and_16 (Op2, selector_1_s5, selector_1_s2);
  and and_17 (and_17_out, selector_1_s4, selector_1_s2);
  DiodeForward diodeforward_3 (.in(and_17_out), .out(Op1));
  DiodeForward diodeforward_4 (.in(and_17_out), .out(Op0));
  PullDown pulldown_1 (.out(Op2));
  and and_18 (Op1, selector_1_s3, selector_1_s2);
  PullDown pulldown_2 (.out(Op1));
  and and_19 (Op0, selector_1_s2, L6);
  PullDown pulldown_3 (.out(Op0));
  and and_20 (and_20_out, selector_1_s1, L6);
  and and_21 (and_21_out, selector_1_s2, L6);
  and and_22 (and_22_out, selector_1_s3, L6);
  or or_6 (Eu, and_27_out, and_26_out, and_25_out, and_24_out, and_23_out, and_22_out, and_21_out, and_20_out);
  and and_23 (and_23_out, selector_1_s4, L6);
  and and_24 (and_24_out, selector_1_s5, L6);
  and and_25 (and_25_out, selector_1_s6, L6);
  and and_26 (and_26_out, selector_1_s0, L6);
  and and_27 (and_27_out, selector_1_s7, L6);
  and and_28 (and_28_out, selector_1_s1, L5);
  nor nor_4 (NLb, and_31_out, and_30_out, and_29_out, and_28_out);
  and and_29 (and_29_out, selector_1_s2, L5);
  and and_30 (and_30_out, selector_1_s4, L5);
  and and_31 (and_31_out, selector_1_s3, L5);
  and and_32 (and_32_out, selector_1_s0, L6);
  and and_33 (and_33_out, selector_1_s1, L6);
  nor nor_5 (NLo, and_38_out, and_37_out, and_36_out, and_35_out, and_34_out, and_33_out, and_32_out);
  and and_34 (and_34_out, selector_1_s2, L6);
  and and_35 (and_35_out, selector_1_s4, L6);
  and and_36 (and_36_out, selector_1_s5, L6);
  and and_37 (and_37_out, selector_1_s6, L6);
  and and_38 (and_38_out, selector_1_s7, L6);
  or or_7 (HLT, ring_counter_1_t7, selector_1_s8);

  assign L1 = Ep;
  assign L2 = Cp;
  assign Op = L4;

  // Notes on the sheet:
  //   FETCH:
  //   T1: PC -> MAR				(Ep, Lm)
  //   T2: Cp++, RAM++			(Cp, WRITE)
  //   T3: RAM -> IR				(READ, Li)
  //   T4: IR -> MAR 				(Ei, Lm)
  //   EXECUTE:
  //   LOAD 0000
  //   T5: RAM -> AC 				(READ, La)
  //   T6: AC -> OUT 				(Ea, Eu, Lo)
  //   T7: HLT
  //   ADD 0001, SUB 0010, MULTI 0100
  //   T5: RAM -> RB 				(READ, Lb)
  //   T6: RB -> ALU -> AC, OUT 		(Eu, La, Lo)
  //   T7: HLT
  //   COMP 0011
  //   T5: RAM -> RB 				(READ, Lb)
  //   T6: RB -> ALU -> AC 			(Eu, La)
  //   T7: HLT
  //   SHIFTR 0101, SHIFTL 0110
  //   T5: RAM -> AC 				(READ, La)
  //   T6: AC -> ALU -> AC, OUT 		(Ea, Eu, La, Lo)
  //   T7: HLT
  //   OUT 1110
  //   T5:
  //   T6: AC -> OUT				(Ea, Eu, Lo)
  //   T7: HLT
  //   000 - Sum
  //   001 - Sub
  //   010 - Comp
  //   011 - Multi
  //   100 - ShiftR
  //   101 - ShiftL
endmodule
