// Digital circuit Instruction Register.dig as structural Verilog
module Instruction_Register (
  input  NEi,
  input  Clr,
  input  Clk,
  input  NLi,
  input  I0,
  input  I1,
  input  I2,
  input  I3,
  input  I4,
  input  I5,
  input  I6,
  input  I7,
  input  Op,
  output C0,
  output C1,
  output C2,
  output C3,
  output Op0,
  output Op1,
  output Op2,
  output Op3
);

  wire not_1_out, not_2_out, register_1_q0, register_1_q1, register_1_q2, register_1_q3;

  not not_1 (not_1_out, NEi);
  not not_2 (not_2_out, NLi);
  Register register_1 (
    .Clk(Clk), .Read(not_1_out), .D0(I0), .Write(not_2_out), .Clr(Clr), .D1(I1), .D2(I2), .D3(I3), .D4(I4),
    .D5(I5), .D6(I6), .D7(I7), .Q0(register_1_q0), .Q1(register_1_q1), .Q2(register_1_q2),
    .Q3(register_1_q3), .Q4(C0), .Q5(C1), .Q6(C2), .Q7(C3));
  assign Op2 = Op ? register_1_q2 : 1'bz;  // Driver driver_1
  assign Op3 = Op ? register_1_q3 : 1'bz;  // Driver driver_2
  assign Op1 = Op ? register_1_q1 : 1'bz;  // Driver driver_3
  assign Op0 = Op ? register_1_q0 : 1'bz;  // Driver driver_4
  PullDown pulldown_1 (.out(Op0));
  PullDown pulldown_2 (.out(Op1));
  PullDown pulldown_3 (.out(Op2));
  PullDown pulldown_4 (.out(Op3));
endmodule
