// Digital circuit MUX.dig as structural Verilog
module MUX (
  input  I0,
  input  A,
  input  I1,
  output S
);

  wire and_1_out, and_2_out, not_1_out;

  not not_1 (not_1_out, A);
  and and_1 (and_1_out, not_1_out, I0);
  and and_2 (and_2_out, not_1_out, I1);
  and and_3 (S, and_1_out, and_2_out);
endmodule
