// Digital circuit Memory Address Register.dig as structural Verilog
module Memory_Address_Register (
  input  NLm,
  input  Clk,
  input  I0,
  input  I1,
  input  I2,
  input  I3,
  input  Clr,
  output S0,
  output S1,
  output S2,
  output S3
);

  wire not_1_out, register_1_q4;

  not not_1 (not_1_out, NLm);
  Register register_1 (
    .Clk(Clk), .Read(1'b1), .D0(I0), .Write(not_1_out), .Clr(Clr), .D1(I1), .D2(I2), .D3(I3), .D4(1'b0),
    .D5(1'b0), .D6(1'b0), .D7(1'b0), .Q0(S0), .Q1(S1), .Q2(S2), .Q3(S3), .Q4(register_1_q4),
    .Q5(register_1_q4), .Q6(register_1_q4), .Q7(register_1_q4));
  // also tied to GND on the sheet: register_1_q4
endmodule
