// Digital circuit Multiplicator.dig as structural Verilog
module Multiplicator (
  input  A0,
  input  B0,
  input  A1,
  input  A2,
  input  A3,
  input  B1
);

  wire and_1_out, and_2_out, and_3_out, and_4_out, and_5_out, and_6_out, and_7_out;

  and and_1 (and_1_out, A0, B0);
  and and_2 (and_2_out, A1, B0);
  and and_3 (and_3_out, A2, B0);
  and and_4 (and_4_out, A3, B0);
  and and_5 (and_5_out, A0, B1);
  and and_6 (and_6_out, A1, B1);
  and and_7 (and_7_out, A2, B1);
  // And and_8 has open pins: In_1=A3, In_2=B1, out=open
  // Adder adder_1: pin names not known; wires that end beside it: and_2_out, and_5_out, and_3_out, and_6_out, and_4_out, and_7_out
endmodule
