// Digital circuit RAM.dig as structural Verilog
module RAM (
  input  I0,
  input  I1,
  input  I2,
  input  I3,
  input  I4,
  input  I5,
  input  I6,
  input  I7,
  input  NCe,
  input  Clr,
  input  Clk,
  input  A,
  input  B,
  input  C,
  input  D,
  output S0,
  output S1,
  output S2,
  output S3,
  output S4,
  output S5,
  output S6,
  output S7
);

  wire and_1_out, and_2_out, and_3_out, and_4_out, and_5_out, and_6_out, and_7_out, and_8_out, and_9_out,
       and_10_out, and_11_out, and_12_out, and_13_out, and_14_out, and_15_out, and_16_out, and_17_out,
       and_18_out, not_1_out, selector_1_s0, selector_1_s1, selector_1_s2, selector_1_s3, selector_1_s4,
       selector_1_s5, selector_1_s6, selector_1_s7, selector_1_s8;

  Selector selector_1 (
    .A(A), .B(B), .C(C), .D(D), .S0(selector_1_s0), .S1(selector_1_s1), .S2(selector_1_s2),
    .S3(selector_1_s3), .S4(selector_1_s4), .S5(selector_1_s5), .S6(selector_1_s6), .S7(selector_1_s7),
    .S8(selector_1_s8));
  not not_1 (not_1_out, NCe);
  and and_1 (and_1_out, not_1_out, selector_1_s0);
  and and_2 (and_2_out, not_1_out, selector_1_s1);
  and and_3 (and_3_out, not_1_out, selector_1_s2);
  and and_4 (and_4_out, not_1_out, selector_1_s3);
  and and_5 (and_5_out, not_1_out, selector_1_s4);
  and and_6 (and_6_out, not_1_out, selector_1_s5);
  and and_7 (and_7_out, not_1_out, selector_1_s6);
  and and_8 (and_8_out, not_1_out, selector_1_s7);
  and and_9 (and_9_out, not_1_out, selector_1_s8);
  and and_10 (and_10_out, not_1_out, selector_1_s0);
  and and_11 (and_11_out, not_1_out, selector_1_s1);
  and and_12 (and_12_out, not_1_out, selector_1_s2);
  and and_13 (and_13_out, not_1_out, selector_1_s3);
  and and_14 (and_14_out, not_1_out, selector_1_s4);
  and and_15 (and_15_out, not_1_out, selector_1_s5);
  and and_16 (and_16_out, not_1_out, selector_1_s6);
  and and_17 (and_17_out, not_1_out, selector_1_s7);
  and and_18 (and_18_out, not_1_out, selector_1_s8);
  Register register_1 (
    .Clk(Clk), .Read(and_10_out), .D0(I0), .Write(and_1_out), .Clr(Clr), .D1(I1), .D2(I2), .D3(I3), .D4(I4),
    .D5(I5), .D6(I6), .D7(I7), .Q0(S0), .Q1(S1), .Q2(S2), .Q3(S3), .Q4(S4), .Q5(S5), .Q6(S6), .Q7(S7));
  Register register_2 (
    .Clk(Clk), .Read(and_11_out), .D0(I0), .Write(and_2_out), .Clr(Clr), .D1(I1), .D2(I2), .D3(I3), .D4(I4),
    .D5(I5), .D6(I6), .D7(I7), .Q0(S0), .Q1(S1), .Q2(S2), .Q3(S3), .Q4(S4), .Q5(S5), .Q6(S6), .Q7(S7));
  Register register_3 (
    .Clk(Clk), .Read(and_12_out), .D0(I0), .Write(and_3_out), .Clr(Clr), .D1(I1), .D2(I2), .D3(I3), .D4(I4),
    .D5(I5), .D6(I6), .D7(I7), .Q0(S0), .Q1(S1), .Q2(S2), .Q3(S3), .Q4(S4), .Q5(S5), .Q6(S6), .Q7(S7));
  Register register_4 (
    .Clk(Clk), .Read(and_13_out), .D0(I0), .Write(and_4_out), .Clr(Clr), .D1(I1), .D2(I2), .D3(I3), .D4(I4),
    .D5(I5), .D6(I6), .D7(I7), .Q0(S0), .Q1(S1), .Q2(S2), .Q3(S3), .Q4(S4), .Q5(S5), .Q6(S6), .Q7(S7));
  Register register_5 (
    .Clk(Clk), .Read(and_14_out), .D0(I0), .Write(and_5_out), .Clr(Clr), .D1(I1), .D2(I2), .D3(I3), .D4(I4),
    .D5(I5), .D6(I6), .D7(I7), .Q0(S0), .Q1(S1), .Q2(S2), .Q3(S3), .Q4(S4), .Q5(S5), .Q6(S6), .Q7(S7));
  Register register_6 (
    .Clk(Clk), .Read(and_15_out), .D0(I0), .Write(and_6_out), .Clr(Clr), .D1(I1), .D2(I2), .D3(I3), .D4(I4),
    .D5(I5), .D6(I6), .D7(I7), .Q0(S0), .Q1(S1), .Q2(S2), .Q3(S3), .Q4(S4), .Q5(S5), .Q6(S6), .Q7(S7));
  Register register_7 (
    .Clk(Clk), .Read(and_16_out), .D0(I0), .Write(and_7_out), .Clr(Clr), .D1(I1), .D2(I2), .D3(I3), .D4(I4),
    .D5(I5), .D6(I6), .D7(I7), .Q0(S0), .Q1(S1), .Q2(S2), .Q3(S3), .Q4(S4), .Q5(S5), .Q6(S6), .Q7(S7));
  Register register_8 (
    .Clk(Clk), .Read(and_17_out), .D0(I0), .Write(and_8_out), .Clr(Clr), .D1(I1), .D2(I2), .D3(I3), .D4(I4),
    .D5(I5), .D6(I6), .D7(I7), .Q0(S0), .Q1(S1), .Q2(S2), .Q3(S3), .Q4(S4), .Q5(S5), .Q6(S6), .Q7(S7));
  Register register_9 (
    .Clk(Clk), .Read(and_18_out), .D0(I0), .Write(and_9_out), .Clr(Clr), .D1(I1), .D2(I2), .D3(I3), .D4(I4),
    .D5(I5), .D6(I6), .D7(I7), .Q0(S0), .Q1(S1), .Q2(S2), .Q3(S3), .Q4(S4), .Q5(S5), .Q6(S6), .Q7(S7));
endmodule
