// Digital circuit Register.dig as structural Verilog
module Register (
  input  Clk,
  input  Read,
  input  D0,
  input  Write,
  input  Clr,
  input  D1,
  input  D2,
  input  D3,
  input  D4,
  input  D5,
  input  D6,
  input  D7,
  output Q0,
  output Q1,
  output Q2,
  output Q3,
  output Q4,
  output Q5,
  output Q6,
  output Q7
);

  wire d_ff_as_1_q, d_ff_as_2_q, d_ff_as_3_q, d_ff_as_4_q, d_ff_as_5_q, d_ff_as_6_q, d_ff_as_7_q,
       d_ff_as_8_q, diodeforward_1_out, diodeforward_2_out, diodeforward_4_out, diodeforward_5_out,
       diodeforward_6_out, diodeforward_8_out, driver_1_out, driver_3_out, driver_5_out, driver_7_out,
       driver_9_out, driver_11_out, driver_13_out, driver_15_out, pulldown_3_out, pulldown_7_out;

  assign driver_1_out = Write ? Clk : 1'bz;  // Driver driver_1
  D_FF_AS d_ff_as_1 (.Set(1'b0), .D(D7), .C(driver_1_out), .Clr(Clr), .Q(d_ff_as_1_q));  // open: nQ
  DiodeForward diodeforward_1 (.in(d_ff_as_1_q), .out(diodeforward_1_out));
  assign Q7 = Read ? diodeforward_1_out : 1'bz;  // Driver driver_2
  PullDown pulldown_1 (.out(diodeforward_1_out));
  assign driver_3_out = Write ? Clk : 1'bz;  // Driver driver_3
  D_FF_AS d_ff_as_2 (.Set(1'b0), .D(D6), .C(driver_3_out), .Clr(Clr), .Q(d_ff_as_2_q));  // open: nQ
  DiodeForward diodeforward_2 (.in(d_ff_as_2_q), .out(diodeforward_2_out));
  assign Q6 = Read ? diodeforward_2_out : 1'bz;  // Driver driver_4
  PullDown pulldown_2 (.out(diodeforward_2_out));
  assign driver_5_out = Write ? Clk : 1'bz;  // Driver driver_5
  D_FF_AS d_ff_as_3 (.Set(1'b0), .D(D5), .C(driver_5_out), .Clr(Clr), .Q(d_ff_as_3_q));  // open: nQ
  PullDown pulldown_3 (.out(pulldown_3_out));
  DiodeForward diodeforward_3 (.in(d_ff_as_3_q), .out(pulldown_3_out));
  assign Q5 = Read ? pulldown_3_out : 1'bz;  // Driver driver_6
  assign driver_7_out = Write ? Clk : 1'bz;  // Driver driver_7
  D_FF_AS d_ff_as_4 (.Set(1'b0), .D(D4), .C(driver_7_out), .Clr(Clr), .Q(d_ff_as_4_q));  // open: nQ
  DiodeForward diodeforward_4 (.in(d_ff_as_4_q), .out(diodeforward_4_out));
  assign Q4 = Read ? diodeforward_4_out : 1'bz;  // Driver driver_8
  PullDown pulldown_4 (.out(diodeforward_4_out));
  assign driver_9_out = Write ? Clk : 1'bz;  // Driver driver_9
  D_FF_AS d_ff_as_5 (.Set(1'b0), .D(D3), .C(driver_9_out), .Clr(Clr), .Q(d_ff_as_5_q));  // open: nQ
  DiodeForward diodeforward_5 (.in(d_ff_as_5_q), .out(diodeforward_5_out));
  assign Q3 = Read ? diodeforward_5_out : 1'bz;  // Driver driver_10
  PullDown pulldown_5 (.out(diodeforward_5_out));
  assign driver_11_out = Write ? Clk : 1'bz;  // Driver driver_11
  D_FF_AS d_ff_as_6 (.Set(1'b0), .D(D2), .C(driver_11_out), .Clr(Clr), .Q(d_ff_as_6_q));  // open: nQ
  DiodeForward diodeforward_6 (.in(d_ff_as_6_q), .out(diodeforward_6_out));
  assign Q2 = Read ? diodeforward_6_out : 1'bz;  // Driver driver_12
  PullDown pulldown_6 (.out(diodeforward_6_out));
  assign driver_13_out = Write ? Clk : 1'bz;  // Driver driver_13
  D_FF_AS d_ff_as_7 (.Set(1'b0), .D(D1), .C(driver_13_out), .Clr(Clr), .Q(d_ff_as_7_q));  // open: nQ
  PullDown pulldown_7 (.out(pulldown_7_out));
  DiodeForward diodeforward_7 (.in(d_ff_as_7_q), .out(pulldown_7_out));
  assign Q1 = Read ? pulldown_7_out : 1'bz;  // Driver driver_14
  assign driver_15_out = Write ? Clk : 1'bz;  // Driver driver_15
  D_FF_AS d_ff_as_8 (.Set(1'b0), .D(D0), .C(driver_15_out), .Clr(Clr), .Q(d_ff_as_8_q));  // open: nQ
  DiodeForward diodeforward_8 (.in(d_ff_as_8_q), .out(diodeforward_8_out));
  assign Q0 = Read ? diodeforward_8_out : 1'bz;  // Driver driver_16
  PullDown pulldown_8 (.out(diodeforward_8_out));
endmodule
