// Digital circuit Ring-Counter.dig as structural Verilog
module Ring_Counter (
  input  Clk,
  input  Ori,
  output T1,
  output T2,
  output T3,
  output T4,
  output T5,
  output T6,
  output T7
);

  wire d_ff_as_1_q, d_ff_as_2_q, d_ff_as_3_q, d_ff_as_4_q, d_ff_as_5_q, d_ff_as_6_q, d_ff_as_7_q, d_ff_as_8_q;

  D_FF_AS d_ff_as_1 (.Set(Ori), .D(d_ff_as_8_q), .C(Clk), .Clr(1'b0), .Q(d_ff_as_1_q));  // open: nQ
  PullDown pulldown_1 (.out(T1));
  DiodeForward diodeforward_1 (.in(d_ff_as_1_q), .out(T1));
  D_FF_AS d_ff_as_2 (.Set(1'b0), .D(d_ff_as_1_q), .C(Clk), .Clr(Ori), .Q(d_ff_as_2_q));  // open: nQ
  PullDown pulldown_2 (.out(T2));
  DiodeForward diodeforward_2 (.in(d_ff_as_2_q), .out(T2));
  D_FF_AS d_ff_as_3 (.Set(1'b0), .D(d_ff_as_2_q), .C(Clk), .Clr(Ori), .Q(d_ff_as_3_q));  // open: nQ
  PullDown pulldown_3 (.out(T3));
  DiodeForward diodeforward_3 (.in(d_ff_as_3_q), .out(T3));
  D_FF_AS d_ff_as_4 (.Set(1'b0), .D(d_ff_as_3_q), .C(Clk), .Clr(Ori), .Q(d_ff_as_4_q));  // open: nQ
  PullDown pulldown_4 (.out(T4));
  DiodeForward diodeforward_4 (.in(d_ff_as_4_q), .out(T4));
  D_FF_AS d_ff_as_5 (.Set(1'b0), .D(d_ff_as_4_q), .C(Clk), .Clr(Ori), .Q(d_ff_as_5_q));  // open: nQ
  PullDown pulldown_5 (.out(T5));
  DiodeForward diodeforward_5 (.in(d_ff_as_5_q), .out(T5));
  D_FF_AS d_ff_as_6 (.Set(1'b0), .D(d_ff_as_5_q), .C(Clk), .Clr(Ori), .Q(d_ff_as_6_q));  // open: nQ
  PullDown pulldown_6 (.out(T6));
  DiodeForward diodeforward_6 (.in(d_ff_as_6_q), .out(T6));
  D_FF_AS d_ff_as_7 (.Set(1'b0), .D(d_ff_as_6_q), .C(Clk), .Clr(Ori), .Q(d_ff_as_7_q));  // open: nQ
  PullDown pulldown_7 (.out(T7));
  DiodeForward diodeforward_7 (.in(d_ff_as_7_q), .out(T7));
  D_FF_AS d_ff_as_8 (.Set(1'b0), .D(d_ff_as_7_q), .C(Clk), .Clr(Ori), .Q(d_ff_as_8_q));  // open: nQ
endmodule
