// Digital circuit Selector.dig as structural Verilog
module Selector (
  input  A,
  input  B,
  input  C,
  input  D,
  output S0,
  output S1,
  output S2,
  output S3,
  output S4,
  output S5,
  output S6,
  output S7,
  output S8
);

  wire not_1_out, not_2_out, not_3_out, not_4_out;

  not not_1 (not_1_out, D);
  not not_2 (not_2_out, C);
  not not_3 (not_3_out, B);
  not not_4 (not_4_out, A);
  and and_1 (S0, not_4_out, not_3_out, not_2_out, not_1_out);
  and and_2 (S1, A, not_3_out, not_2_out, not_1_out);
  and and_3 (S2, not_4_out, B, not_2_out, not_1_out);
  and and_4 (S3, A, B, not_2_out, not_1_out);
  and and_5 (S4, C, not_4_out, not_3_out, not_1_out);
  and and_6 (S5, A, not_3_out, C, not_1_out);
  and and_7 (S6, not_4_out, B, C, not_1_out);
  and and_8 (S7, A, B, C, not_1_out);
  and and_9 (S8, not_4_out, not_3_out, not_2_out, D);

  // Notes on the sheet:
  //   0000
  //   0001
  //   0010
  //   0011
  //   0100
  //   0101
  //   0110
  //   0111
  //   1000
endmodule
