// Digital circuit ULA.dig as structural Verilog
module ULA (
  input  A0,
  input  B0,
  input  A1,
  input  B1,
  input  A2,
  input  B2,
  input  A3,
  input  B3,
  input  A4,
  input  B4,
  input  A5,
  input  B5,
  input  A6,
  input  B6,
  input  A7,
  input  B7,
  input  C0,
  input  C1,
  input  C2,
  input  Eu,
  output out_20,
  output eq,
  output plus,
  output S0,
  output S1,
  output S2,
  output S3,
  output S4,
  output S5,
  output S6,
  output S7
);

  wire adder_1_ov, adder_1_s0, adder_1_s1, adder_1_s2, adder_1_s3, adder_1_s4, adder_1_s5, adder_1_s6,
       adder_1_s7, bit_shifter_1_p10, bit_shifter_1_p11, bit_shifter_1_p12, bit_shifter_1_p13,
       bit_shifter_1_p14, bit_shifter_1_p15, bit_shifter_1_p16, bit_shifter_1_p17, comparator_1_a_eq_b,
       comparator_1_a_gt_b, comparator_1_a_lt_b, diodeforward_1_out, diodeforward_3_out, diodeforward_4_out,
       diodeforward_5_out, diodeforward_6_out, diodeforward_7_out, diodeforward_8_out, diodeforward_9_out,
       diodeforward_10_out, driver_1_out, driver_2_out, driver_3_out, driver_4_out, driver_5_out,
       driver_6_out, driver_8_out, driver_9_out, driver_10_out, driver_11_out, driver_12_out, driver_13_out,
       driver_14_out, driver_15_out, driver_16_out, driver_17_out, driver_18_out, driver_19_out,
       driver_20_out, driver_21_out, driver_22_out, driver_23_out, driver_24_out, driver_25_out,
       driver_26_out, driver_27_out, driver_28_out, driver_29_out, driver_30_out, driver_31_out,
       driver_32_out, driver_33_out, driver_34_out, driver_35_out, driver_36_out, driver_37_out,
       driver_38_out, multiplicator_1_s0, multiplicator_1_s1, multiplicator_1_s2, multiplicator_1_s3,
       multiplicator_1_s4, multiplicator_1_s5, multiplicator_1_s6, multiplicator_1_s7, selector_1_s0,
       selector_1_s1, selector_1_s2, selector_1_s3, selector_1_s4, selector_1_s5, selector_1_s6,
       subtractor_1_s0, subtractor_1_s1, subtractor_1_s2, subtractor_1_s3, subtractor_1_s4, subtractor_1_s5,
       subtractor_1_s6, subtractor_1_s7, subtractor_1_sig;

  Selector selector_1 (
    .A(C0), .B(C1), .C(C2), .D(selector_1_s6), .S0(selector_1_s0), .S1(selector_1_s1), .S2(selector_1_s2),
    .S3(selector_1_s3), .S4(selector_1_s4), .S5(selector_1_s5), .S6(selector_1_s6), .S7(selector_1_s6),
    .S8(selector_1_s6));
  DiodeForward diodeforward_1 (.in(selector_1_s4), .out(diodeforward_1_out));
  DiodeForward diodeforward_2 (.in(selector_1_s5), .out(diodeforward_1_out));
  PullDown pulldown_1 (.out(diodeforward_1_out));
  Adder adder_1 (
    .A0(A0), .B0(B0), .A1(A1), .B1(B1), .A2(A2), .B2(B2), .A3(A3), .B3(B3), .A4(A4), .B4(B4), .A5(A5),
    .B5(B5), .A6(A6), .B6(B6), .A7(A7), .B7(B7), .S0(adder_1_s0), .S1(adder_1_s1), .S2(adder_1_s2),
    .S3(adder_1_s3), .S4(adder_1_s4), .S5(adder_1_s5), .S6(adder_1_s6), .S7(adder_1_s7), .Ov(adder_1_ov));
  Subtractor subtractor_1 (
    .A0(A0), .B0(B0), .A1(A1), .B1(B1), .A2(A2), .B2(B2), .A3(A3), .B3(B3), .A4(A4), .B4(B4), .A5(A5),
    .B5(B5), .A6(A6), .B6(B6), .A7(A7), .B7(B7), .S0(subtractor_1_s0), .S1(subtractor_1_s1),
    .S2(subtractor_1_s2), .S3(subtractor_1_s3), .S4(subtractor_1_s4), .S5(subtractor_1_s5),
    .S6(subtractor_1_s6), .S7(subtractor_1_s7), .Sig(subtractor_1_sig));
  Comparator comparator_1 (
    .A0(A0), .B0(B0), .A1(A1), .A2(A2), .A3(A3), .A4(A4), .A5(A5), .A6(A6), .A7(A7), .B1(B1), .B2(B2),
    .B3(B3), .B4(B4), .B5(B5), .B6(B6), .B7(B7), .A_lt_B(comparator_1_a_lt_b), .A_eq_B(comparator_1_a_eq_b),
    .A_gt_B(comparator_1_a_gt_b));
  // Bit_Shifter bit_shifter_1: pin names not known; wires that end beside it: A0, selector_1_s4, A1, A2, A3, A4, A5, A6, A7, bit_shifter_1_p10, bit_shifter_1_p11, bit_shifter_1_p12, bit_shifter_1_p13, bit_shifter_1_p14, bit_shifter_1_p15, bit_shifter_1_p16, bit_shifter_1_p17
  Multiplicator multiplicator_1 (
    .A0(A0), .A1(A1), .A2(A2), .A3(A3), .B0(B0), .B1(B1), .B2(B2), .B3(B3), .S0(multiplicator_1_s0),
    .S1(multiplicator_1_s1), .S2(multiplicator_1_s2), .S3(multiplicator_1_s3), .S4(multiplicator_1_s4),
    .S5(multiplicator_1_s5), .S6(multiplicator_1_s6), .S7(multiplicator_1_s7));
  assign driver_1_out = selector_1_s0 ? adder_1_ov : 1'bz;  // Driver driver_1
  assign driver_2_out = selector_1_s1 ? subtractor_1_sig : 1'bz;  // Driver driver_2
  assign driver_3_out = selector_1_s0 ? adder_1_s7 : 1'bz;  // Driver driver_3
  assign driver_4_out = selector_1_s1 ? subtractor_1_s7 : 1'bz;  // Driver driver_4
  assign driver_5_out = diodeforward_1_out ? bit_shifter_1_p17 : 1'bz;  // Driver driver_5
  assign driver_6_out = selector_1_s3 ? multiplicator_1_s7 : 1'bz;  // Driver driver_6
  assign driver_6_out = selector_1_s3 ? multiplicator_1_s7 : 1'bz;  // Driver driver_7
  assign driver_8_out = selector_1_s0 ? adder_1_s6 : 1'bz;  // Driver driver_8
  assign driver_9_out = selector_1_s1 ? subtractor_1_s6 : 1'bz;  // Driver driver_9
  assign driver_10_out = diodeforward_1_out ? bit_shifter_1_p16 : 1'bz;  // Driver driver_10
  assign driver_11_out = selector_1_s3 ? multiplicator_1_s6 : 1'bz;  // Driver driver_11
  assign driver_12_out = selector_1_s0 ? adder_1_s5 : 1'bz;  // Driver driver_12
  assign driver_13_out = selector_1_s1 ? subtractor_1_s5 : 1'bz;  // Driver driver_13
  assign driver_14_out = diodeforward_1_out ? bit_shifter_1_p15 : 1'bz;  // Driver driver_14
  assign driver_15_out = selector_1_s3 ? multiplicator_1_s5 : 1'bz;  // Driver driver_15
  assign driver_16_out = selector_1_s0 ? adder_1_s4 : 1'bz;  // Driver driver_16
  assign driver_17_out = selector_1_s1 ? subtractor_1_s4 : 1'bz;  // Driver driver_17
  assign driver_18_out = diodeforward_1_out ? bit_shifter_1_p14 : 1'bz;  // Driver driver_18
  assign driver_19_out = selector_1_s3 ? multiplicator_1_s4 : 1'bz;  // Driver driver_19
  assign driver_20_out = selector_1_s0 ? adder_1_s3 : 1'bz;  // Driver driver_20
  assign driver_21_out = selector_1_s1 ? subtractor_1_s3 : 1'bz;  // Driver driver_21
  assign driver_22_out = diodeforward_1_out ? bit_shifter_1_p13 : 1'bz;  // Driver driver_22
  assign driver_23_out = selector_1_s3 ? multiplicator_1_s3 : 1'bz;  // Driver driver_23
  assign driver_24_out = selector_1_s0 ? adder_1_s2 : 1'bz;  // Driver driver_24
  assign driver_25_out = selector_1_s1 ? subtractor_1_s2 : 1'bz;  // Driver driver_25
  assign driver_26_out = selector_1_s2 ? comparator_1_a_gt_b : 1'bz;  // Driver driver_26
  assign driver_27_out = diodeforward_1_out ? bit_shifter_1_p12 : 1'bz;  // Driver driver_27
  assign driver_28_out = selector_1_s3 ? multiplicator_1_s2 : 1'bz;  // Driver driver_28
  assign driver_29_out = selector_1_s0 ? adder_1_s1 : 1'bz;  // Driver driver_29
  assign driver_30_out = selector_1_s1 ? subtractor_1_s1 : 1'bz;  // Driver driver_30
  assign driver_31_out = selector_1_s2 ? comparator_1_a_eq_b : 1'bz;  // Driver driver_31
  assign driver_32_out = diodeforward_1_out ? bit_shifter_1_p11 : 1'bz;  // Driver driver_32
  assign driver_33_out = selector_1_s3 ? multiplicator_1_s1 : 1'bz;  // Driver driver_33
  assign driver_34_out = selector_1_s0 ? adder_1_s0 : 1'bz;  // Driver driver_34
  assign driver_35_out = selector_1_s1 ? subtractor_1_s0 : 1'bz;  // Driver driver_35
  assign driver_36_out = selector_1_s2 ? comparator_1_a_lt_b : 1'bz;  // Driver driver_36
  assign driver_37_out = diodeforward_1_out ? bit_shifter_1_p10 : 1'bz;  // Driver driver_37
  assign driver_38_out = selector_1_s3 ? multiplicator_1_s0 : 1'bz;  // Driver driver_38
  DiodeForward diodeforward_3 (.in(driver_34_out), .out(diodeforward_3_out));
  DiodeForward diodeforward_4 (.in(driver_29_out), .out(diodeforward_4_out));
  DiodeForward diodeforward_5 (.in(driver_24_out), .out(diodeforward_5_out));
  DiodeForward diodeforward_6 (.in(driver_20_out), .out(diodeforward_6_out));
  DiodeForward diodeforward_7 (.in(driver_16_out), .out(diodeforward_7_out));
  DiodeForward diodeforward_8 (.in(driver_12_out), .out(diodeforward_8_out));
  DiodeForward diodeforward_9 (.in(driver_8_out), .out(diodeforward_9_out));
  DiodeForward diodeforward_10 (.in(driver_3_out), .out(diodeforward_10_out));
  DiodeForward diodeforward_11 (.in(driver_1_out), .out(plus));
  DiodeForward diodeforward_12 (.in(driver_35_out), .out(diodeforward_3_out));
  DiodeForward diodeforward_13 (.in(driver_30_out), .out(diodeforward_4_out));
  DiodeForward diodeforward_14 (.in(driver_25_out), .out(diodeforward_5_out));
  DiodeForward diodeforward_15 (.in(driver_21_out), .out(diodeforward_6_out));
  DiodeForward diodeforward_16 (.in(driver_17_out), .out(diodeforward_7_out));
  DiodeForward diodeforward_17 (.in(driver_13_out), .out(diodeforward_8_out));
  DiodeForward diodeforward_18 (.in(driver_9_out), .out(diodeforward_9_out));
  DiodeForward diodeforward_19 (.in(driver_4_out), .out(diodeforward_10_out));
  DiodeForward diodeforward_20 (.in(driver_2_out), .out(out_20));
  DiodeForward diodeforward_21 (.in(driver_36_out), .out(out_20));
  DiodeForward diodeforward_22 (.in(driver_31_out), .out(eq));
  DiodeForward diodeforward_23 (.in(driver_26_out), .out(plus));
  DiodeForward diodeforward_24 (.in(driver_37_out), .out(diodeforward_3_out));
  DiodeForward diodeforward_25 (.in(driver_32_out), .out(diodeforward_4_out));
  DiodeForward diodeforward_26 (.in(driver_27_out), .out(diodeforward_5_out));
  DiodeForward diodeforward_27 (.in(driver_22_out), .out(diodeforward_6_out));
  DiodeForward diodeforward_28 (.in(driver_18_out), .out(diodeforward_7_out));
  DiodeForward diodeforward_29 (.in(driver_14_out), .out(diodeforward_8_out));
  DiodeForward diodeforward_30 (.in(driver_10_out), .out(diodeforward_9_out));
  DiodeForward diodeforward_31 (.in(driver_5_out), .out(diodeforward_10_out));
  DiodeForward diodeforward_32 (.in(driver_38_out), .out(diodeforward_3_out));
  DiodeForward diodeforward_33 (.in(driver_33_out), .out(diodeforward_4_out));
  DiodeForward diodeforward_34 (.in(driver_28_out), .out(diodeforward_5_out));
  DiodeForward diodeforward_35 (.in(driver_23_out), .out(diodeforward_6_out));
  DiodeForward diodeforward_36 (.in(driver_19_out), .out(diodeforward_7_out));
  DiodeForward diodeforward_37 (.in(driver_15_out), .out(diodeforward_8_out));
  DiodeForward diodeforward_38 (.in(driver_11_out), .out(diodeforward_9_out));
  DiodeForward diodeforward_39 (.in(driver_6_out), .out(diodeforward_10_out));
  PullDown pulldown_2 (.out(out_20));
  PullDown pulldown_3 (.out(eq));
  PullDown pulldown_4 (.out(plus));
  assign S4 = Eu ? diodeforward_7_out : 1'bz;  // Driver driver_39
  assign S5 = Eu ? diodeforward_8_out : 1'bz;  // Driver driver_40
  assign S6 = Eu ? diodeforward_9_out : 1'bz;  // Driver driver_41
  assign S7 = Eu ? diodeforward_10_out : 1'bz;  // Driver driver_42
  assign S1 = Eu ? diodeforward_4_out : 1'bz;  // Driver driver_43
  assign S2 = Eu ? diodeforward_5_out : 1'bz;  // Driver driver_44
  assign S3 = Eu ? diodeforward_6_out : 1'bz;  // Driver driver_45
  PullDown pulldown_5 (.out(diodeforward_3_out));
  PullDown pulldown_6 (.out(diodeforward_4_out));
  PullDown pulldown_7 (.out(diodeforward_5_out));
  PullDown pulldown_8 (.out(diodeforward_6_out));
  PullDown pulldown_9 (.out(diodeforward_7_out));
  PullDown pulldown_10 (.out(diodeforward_8_out));
  PullDown pulldown_11 (.out(diodeforward_9_out));
  PullDown pulldown_12 (.out(diodeforward_10_out));
  PullDown pulldown_13 (.out(plus));
  assign S0 = Eu ? diodeforward_3_out : 1'bz;  // Driver driver_46
  // also tied to GND on the sheet: selector_1_s6

  // Notes on the sheet:
  //   C0: 000 - Sum
  //   001 - Sub
  //   010 - Comp
  //   011 - Multi
  //   100 - ShiftR
  //   101 - ShiftL
  //   C1: 000 - Sum
  //   001 - Sub
  //   010 - Comp
  //   011 - Multi
  //   100 - ShiftR
  //   101 - ShiftL
  //   C2: 000 - Sum
  //   001 - Sub
  //   010 - Comp
  //   011 - Multi
  //   100 - ShiftR
  //   101 - ShiftL
  //   000 - Sum
  //   001 - Sub
  //   010 - Comp
  //   011 - Multi
  //   100 - ShiftR
  //   101 - ShiftL
endmodule
